# Fritzing sketch intel-edison-lcd-buttons (saved by Fritzing 0.9.3b)
breadboards: 1

parts:
  LCD3 = LCD screen
  S4 = Pushbutton [part_number=otherBtn package="[THT]"]
  R3 = Resistor [tolerance=±5% resistance=220 package=THT]
  S5 = Pushbutton [part_number=goBtn package="[THT]"]
  R4 = Resistor [tolerance=±5% resistance=220 package=THT]
  R5 = TSR-3386UT Square Trimming Potentiometer [part_number=TSR-3386]
  S6 = Pushbutton [part_number=downBtn package="[THT]"]
  S7 = Pushbutton [part_number=upBtn package="[THT]"]
  S8 = Pushbutton [part_number=metaBtn package="[THT]"]
  R6 = Resistor [tolerance=±5% resistance=220 package=THT]
  R7 = Resistor [tolerance=±5% resistance=220 package=THT]
  LED1 = LED - 5mm [color="Blue (470nm)" package="5 mm [THT]"]
  R8 = Resistor [tolerance=±5% resistance=100 package=THT]
  R9 = Resistor [tolerance=±5% resistance=220 package=THT]
  Part7 = Intel Edison

nets:
  VSS: LCD3.VSS, LCD3.R/W, LCD3.LED-, R3.Pin_0, R4.Pin_0, R5.Leg2, R6.Pin_0, R7.Pin_0, R8.Pin_0, R9.Pin_0, Part7.GND
  VDD: LCD3.VDD, LCD3.LED+, S4.Pin_1, S4.Pin_2, S5.Pin_1, S5.Pin_2, R5.Leg1, S6.Pin_1, S6.Pin_2, S7.Pin_1, S7.Pin_2, S8.Pin_1, S8.Pin_2, Part7.5V
  N1: LCD3.V0, R5.wiper
  N2: LCD3.RS, Part7.D7
  N3: LCD3.E, Part7.D8
  N4: LCD3.DB4, Part7.D9_PWM
  N5: LCD3.DB5, Part7.D10_PWM/SS
  N6: LCD3.DB6, Part7.D11_PWM/MOSI
  N7: LCD3.DB7, Part7.D12/MISO
  N8: S4.Pin_3, S4.Pin_4, Part7.D3_PWM
  N9: S5.Pin_3, S5.Pin_4, Part7.D2
  N10: S6.Pin_3, S6.Pin_4, Part7.D4
  N11: S7.Pin_3, S7.Pin_4, Part7.D6_PWM
  N12: S8.Pin_3, S8.Pin_4, Part7.D13/SCK
  N13: LED1.anode, Part7.D5_PWM

notes:
  downBtn and upBtn: use to remove or add time from/to the current pom
  goBtn is righthand meta button
  otherBtn is lefthand meta button
  metaBtn toggles details display (total poms and minutes)

custom parts:
  LCD screen: A standard character display, usually with 2x16 characters. Comes in many colors.
  TSR-3386UT Square Trimming Potentiometer: Trimpot 10K with Knob
  Intel Edison: The Intel® Edison development platform is designed to lower the barriers to entry for a range of inventors, entrepreneurs, and consumer product designers to rapidly prototype and produce “Internet of Things” (IoT) and wearable computing products.
